// Logisim project lab1.circ as structural Verilog: 6 circuits, main circuit Main
module Main (
);

  wire Clock;
  wire [1:0] ROMSimpleCombinationalOutput;
  wire [2:0] CombinationalOutput, ROMCombinationalOutput;
  wire [3:0] SimpleInput;
  wire [7:0] Input;

  Combinational_Input combinational_input_1 (
    .In7(Input[7]), .In6(Input[6]), .In5(Input[5]), .In4(Input[4]), .In3(Input[3]), .In2(Input[2]),
    .In1(Input[1]), .In0(Input[0]), .Clock(Clock));
  Simple_Combinational_Input simple_combinational_input_1 (
    .In3(SimpleInput[3]), .In2(SimpleInput[2]), .In1(SimpleInput[1]), .In0(SimpleInput[0]), .Clock(Clock));
  Clock clock_1 (.out(Clock));
  _1__Combinatorial_Circuit___Combinational_Logic u_1_combinatorial_circuit_combinational_logic_1 (
    .In7(Input[7]), .In6(Input[6]), .In5(Input[5]), .In4(Input[4]), .In3(Input[3]), .In2(Input[2]),
    .In1(Input[1]), .In0(Input[0]), .Out2(CombinationalOutput[2]), .Out1(CombinationalOutput[1]),
    .Out0(CombinationalOutput[0]));
  _2__Small_Combinational_Circuit___ROM u_2_small_combinational_circuit_rom_1 (
    .In3(SimpleInput[3]), .In2(SimpleInput[2]), .In1(SimpleInput[1]), .In0(SimpleInput[0]),
    .Out1(ROMSimpleCombinationalOutput[1]), .Out0(ROMSimpleCombinationalOutput[0]));
  _3__Large_Combinational_Circuit u_3_large_combinational_circuit_1 (
    .In7(Input[7]), .In6(Input[6]), .In5(Input[5]), .In4(Input[4]), .In3(Input[3]), .In2(Input[2]),
    .In1(Input[1]), .In0(Input[0]), .Out2(ROMCombinationalOutput[2]), .Out1(ROMCombinationalOutput[1]),
    .Out0(ROMCombinationalOutput[0]));
  // Probe on Input
  // Probe on SimpleInput
  // Probe on CombinationalOutput
  // Probe on ROMSimpleCombinationalOutput
  // Probe on ROMCombinationalOutput
endmodule

module Combinational_Input (
  input  Clock,
  output In7,
  output In6,
  output In5,
  output In4,
  output In3,
  output In2,
  output In1,
  output In0
);

  Counter #(.ongoal("stay")) counter_1 (
    .count(1'b1), .Q({In7, In6, In5, In4, In3, In2, In1, In0}), .clk(Clock));  // open: load, D, carry, clr
endmodule

module Simple_Combinational_Input (
  input  Clock,
  output In3,
  output In2,
  output In1,
  output In0
);

  Counter #(.width(4), .max('hf), .ongoal("stay")) counter_1 (
    .count(1'b1), .Q({In3, In2, In1, In0}), .clk(Clock));  // open: load, D, carry, clr
endmodule

// Com
module _1__Combinatorial_Circuit___Combinational_Logic (
  input  In7,
  input  In6,
  input  In5,
  input  In4,
  input  In3,
  input  In2,
  input  In1,
  input  In0,
  output Out2,
  output Out1,
  output Out0
);

  wire and_1_out, and_2_out, and_3_out, and_4_out, and_5_out, and_6_out, and_7_out, and_8_out, and_9_out,
       and_10_out, and_11_out, and_12_out, and_13_out, not_1_out, not_2_out, not_3_out, not_4_out, not_5_out,
       not_6_out, not_7_out, not_8_out, not_9_out, not_10_out, not_11_out, not_12_out, not_13_out,
       not_14_out, not_15_out, not_16_out, not_17_out, not_18_out, not_19_out, not_20_out, not_21_out,
       not_22_out, not_23_out, not_24_out, not_25_out, not_26_out, not_27_out, not_28_out, not_29_out;

  not not_1 (not_1_out, In5);
  not not_2 (not_2_out, In4);
  not not_3 (not_3_out, In3);
  not not_4 (not_4_out, In0);
  not not_5 (not_5_out, In5);
  not not_6 (not_6_out, In4);
  not not_7 (not_7_out, In1);
  not not_8 (not_8_out, In6);
  not not_9 (not_9_out, In4);
  not not_10 (not_10_out, In2);
  not not_11 (not_11_out, In5);
  not not_12 (not_12_out, In4);
  not not_13 (not_13_out, In1);
  not not_14 (not_14_out, In7);
  not not_15 (not_15_out, In6);
  not not_16 (not_16_out, In2);
  and and_1 (and_1_out, not_16_out, In0);
  not not_17 (not_17_out, In2);
  and and_2 (and_2_out, not_17_out, In1);
  not not_18 (not_18_out, In3);
  and and_3 (and_3_out, not_18_out, In2, not_19_out);
  not not_19 (not_19_out, In1);
  and and_4 (and_4_out, In3, In1);
  not not_20 (not_20_out, In5);
  not not_21 (not_21_out, In4);
  not not_22 (not_22_out, In3);
  not not_23 (not_23_out, In1);
  not not_24 (not_24_out, In0);
  not not_25 (not_25_out, In7);
  not not_26 (not_26_out, In4);
  not not_27 (not_27_out, In1);
  not not_28 (not_28_out, In7);
  not not_29 (not_29_out, In4);
  and and_5 (and_5_out, not_1_out, not_2_out, not_3_out, In1, not_4_out);
  and and_6 (and_6_out, not_5_out, not_6_out, In2, not_7_out, In0);
  and and_7 (and_7_out, not_8_out, not_9_out, In3, not_10_out);
  and and_8 (and_8_out, not_11_out, not_12_out, In3, not_13_out);
  and and_9 (and_9_out, not_14_out, In5);
  and and_10 (and_10_out, In7, not_15_out);
  and and_11 (and_11_out, not_20_out, not_21_out, not_22_out, not_23_out, not_24_out);
  and and_12 (and_12_out, not_25_out, not_26_out, In2, not_27_out);
  and and_13 (and_13_out, not_28_out, not_29_out, In3, In1);
  or or_1 (Out2, and_5_out, and_6_out, and_7_out, and_8_out, and_9_out, and_10_out);
  or or_2 (Out1, and_1_out, and_2_out, and_3_out, and_4_out, In4, In5);
  or or_3 (Out0, and_11_out, and_12_out, and_13_out, In6);
endmodule

module _2__Small_Combinational_Circuit___ROM (
  input  In3,
  input  In2,
  input  In1,
  input  In0,
  output Out1,
  output Out0
);

  ROM #(.addrWidth(4), .dataWidth(2)) rom_1 (.addr({In3, In2, In1, In0}), .data({Out1, Out0}));  // open: sel

  // Notes on the sheet:
  //   contents of rom_1 (hex, n*v repeats v):
  //   3 2 1 3 2 1 3 3 3 0 3 0 2 0 3
endmodule

module _3__Large_Combinational_Circuit (
  input  In7,
  input  In6,
  input  In5,
  input  In4,
  input  In3,
  input  In2,
  input  In1,
  input  In0,
  output Out2,
  output Out1,
  output Out0
);

  ROM #(.dataWidth(3)) rom_1 (.addr({In7, In6, In5, In4, In3, In2, In1, In0}), .data({Out2, Out1, Out0}));  // open: sel

  // Notes on the sheet:
  //   contents of rom_1 (hex, n*v repeats v):
  //   1 2 6 2 3 7 4 0 4 0 7 0 5 0 3 0 16*2 64*0 16*7 48*0 16*6 48*0 16*3
endmodule
