// Logisim project Lab 2.circ as structural Verilog: 7 circuits, main circuit Main
module Main (
);

  wire BSel, clock_1_out, clock_2_out, clock_3_out, Immediate, MemRd, MemWr, WrReg, Zero;
  wire [1:0] DataSel, PCSel, RegSel;
  wire [2:0] ALUctl;
  wire [4:0] rs, rt, WrAddr;
  wire [5:0] Opcode;
  wire [15:0] addr;
  wire [31:0] addr_4, ALUResult, B, Branch, DataExt, MemData, NewPC, PC, PC_4, RdData1, RdData2, WriteData;

  // Probe on Opcode
  // Probe on addr[5:0]
  Adder #(.width(32)) adder_1 (.a(addr_4), .b(PC_4), .out(Branch));  // open: cin, cout
  Shifter #(.width(32)) shifter_1 (.in(DataExt), .\dist (5'b00010), .out(addr_4));
  Adder #(.width(32)) adder_2 (.a(32'h4), .b(PC), .out(PC_4));  // open: cin, cout
  Register #(.width(32)) u_PC (.D(NewPC), .Q(PC), .clk(clock_1_out));  // open: en, clr
  Clock clock_1 (.out(clock_1_out));
  Control_Unit control_unit_1 (
    .Opcode(Opcode), .Func(addr[5:0]), .ALUCtl(ALUctl), .MemWr(MemWr), .MemRd(MemRd), .Immediate(Immediate),
    .WrReg(WrReg), .RegSel(RegSel), .PCSel(PCSel), .DataSel(DataSel), .zero(Zero), .BSel(BSel));
  // Probe on PC[9:2]
  Multiplexer #(.select(2), .width(32)) multiplexer_1 (
    .in0(PC_4), .in1(Branch), .in2(addr_4), .in3(RdData1), .out(NewPC), .sel(PCSel));  // open: en
  ROM #(.dataWidth(32)) rom_1 (.addr(PC[9:2]), .data({Opcode, rs, rt, addr}));  // open: sel
  // Probe on rs
  // Probe on rt
  Register_File register_file_1 (
    .WrAddr(WrAddr), .WrData(WriteData), .WrReg(WrReg), .RdAddr1(rs), .RdAddr2(rt), .RdData1(RdData1),
    .RdData2(RdData2), .Clock(clock_2_out));
  Clock clock_2 (.out(clock_2_out));
  // Probe on addr
  // Probe on addr[15:11]
  // Probe on rt
  Multiplexer #(.select(2), .width(5)) multiplexer_2 (
    .in0(addr[15:11]), .in1(rt), .in2({5{1'b1}}), .out(WrAddr), .sel(RegSel));  // open: in3, en
  // Probe on MemWr
  ALU alu_1 (
    .ALUCtl(ALUctl), .A(RdData1), .B(B), .ALUResult(ALUResult), .Zero(Zero), .Shamt({5{1'b0}}));  // open: Overflow
  Clock clock_3 (.out(clock_3_out));
  // Probe on ALUctl
  // Probe on ALUResult
  Multiplexer #(.select(2), .width(32)) multiplexer_3 (
    .in0(ALUResult), .in1(MemData), .in2(PC_4), .out(WriteData), .sel(DataSel));  // open: in3, en
  RAM #(.dataWidth(32), .bus("separate")) ram_1 (
    .addr(ALUResult[9:2]), .din(RdData2), .data(MemData), .str(MemWr), .clk(clock_3_out), .ld(MemRd));  // open: sel, clr
  // Probe on MemData
  assign DataExt = {{16{1'b0}}, addr};  // Bit_Extender bit_extender_1
  // Probe on B
  Multiplexer #(.width(32)) multiplexer_4 (.in0(RdData2), .in1(DataExt), .out(B), .sel(BSel));  // open: en
  // Probe on WrAddr
  // Probe on WriteData
  // Probe on WrReg
  // Probe on PC
  // Probe on NewPC
  // Probe on RdData1
  // Probe on RdData2
  // Probe on MemData
  // Probe on Branch

  // Other names for the same wires on the sheet: func[5:0] = addr[5:0]; rd[4:0] = addr[15:11]

  // Notes on the sheet:
  //   Intruction Mem
  //   PC selection
  //   contents of rom_1 (hex, n*v repeats v):
  //   20010008 34220005 3043ffff 612020 832822 223024 c33826 aca40064 8ca80064 22482a 1265025 c00000d
  //   200b0001 23ff0018 10c00003 a13022 800000e 200c0001 3e00008 200d0001 200e0001
  //   WrReg selection
  //   WriteData seletion
  //   Data Mem
  //   Data to ALU
endmodule

module ALU (
  input  [2:0] ALUCtl,
  input  [31:0] A,
  input  [31:0] B,
  input  [4:0] Shamt,
  output [31:0] ALUResult,
  output Zero,
  output Overflow
);

  wire comparator_1_lt, comparator_2_lt, comparator_3_eq, comparator_4_eq, or_2_out;
  wire [31:0] ADD, AND, NOR, OR, SLL, SLT, SLTU, SRL, SUB, XOR;

  // Probe on ALUCtl
  assign NOR = ~(A | B);  // NOR_Gate nor_1, 32 bits wide
  Adder #(.width(32)) adder_1 (.a(A), .b(B), .out(ADD));  // open: cin, cout
  Subtractor #(.width(32)) subtractor_1 (.a(A), .b(B), .out(SUB));  // open: bin, bout
  assign AND = A & B;  // AND_Gate and_1, 32 bits wide
  assign OR = A | B;  // OR_Gate or_1, 32 bits wide
  assign XOR = A ^ B;  // XOR_Gate xor_1, 32 bits wide
  Comparator #(.width(32)) comparator_1 (.a(A), .b(B), .lt(comparator_1_lt));  // open: gt, eq
  assign SLT = {{31{1'b0}}, comparator_1_lt};  // Bit_Extender bit_extender_1
  Shifter #(.width(32)) shifter_1 (.in(B), .\dist (Shamt), .out(SLL));
  Shifter #(.width(32), .shift("lr")) shifter_2 (.in(B), .\dist (Shamt), .out(SRL));
  Comparator #(.width(32), .mode("unsigned")) comparator_2 (.a(A), .b(B), .lt(comparator_2_lt));  // open: gt, eq
  assign SLTU = {{31{1'b0}}, comparator_2_lt};  // Bit_Extender bit_extender_2
  Multiplexer #(.select(3), .width(32), .enable("false")) multiplexer_1 (
    .in0(AND), .in1(ADD), .in2(OR), .in3(SUB), .in4(SLT), .in5(XOR), .out(ALUResult), .sel(ALUCtl));  // open: in6, in7
  Comparator #(.width(3)) comparator_3 (.a(3'b001), .b(ALUCtl), .eq(comparator_3_eq));  // open: gt, lt
  Comparator #(.width(3)) comparator_4 (.a(ALUCtl), .b(3'b011), .eq(comparator_4_eq));  // open: gt, lt
  Overflow_Unit overflow_unit_1 (
    .Add(comparator_3_eq), .Sub(comparator_4_eq), .ASign(A[31]), .BSign(B[31]), .ResultSign(ALUResult[31]),
    .Overflow(Overflow));
  or or_2 (or_2_out, ALUResult[0], ALUResult[1], ALUResult[2], ALUResult[3], ALUResult[4], ALUResult[5], ALUResult[6], ALUResult[7], ALUResult[8], ALUResult[9], ALUResult[10], ALUResult[11], ALUResult[12], ALUResult[13], ALUResult[14], ALUResult[15], ALUResult[16], ALUResult[17], ALUResult[18], ALUResult[19], ALUResult[20], ALUResult[21], ALUResult[22], ALUResult[23], ALUResult[24], ALUResult[25], ALUResult[26], ALUResult[27], ALUResult[28], ALUResult[29], ALUResult[30], ALUResult[31]);
  not not_1 (Zero, or_2_out);

  // Other names for the same wires on the sheet: ASign = A[31]; ResultSign = ALUResult[31]; BSign = B[31]

  // Notes on the sheet:
  //   ALUCtl for ADD for top port
  //   ALUCtl for SUB for second port
endmodule

module Register_File (
  input  [4:0] WrAddr,
  input  [31:0] WrData,
  input  WrReg,
  input  [4:0] RdAddr1,
  input  [4:0] RdAddr2,
  input  Clock,
  output [31:0] RdData1,
  output [31:0] RdData2
);

  wire WrReg0, WrReg1, WrReg2, WrReg3, WrReg4, WrReg5, WrReg6, WrReg7, WrReg8, WrReg9, WrReg10, WrReg11,
       WrReg12, WrReg13, WrReg14, WrReg15, WrReg16, WrReg17, WrReg18, WrReg19, WrReg20, WrReg21, WrReg22,
       WrReg23, WrReg24, WrReg25, WrReg26, WrReg27, WrReg28, WrReg29, WrReg30, WrReg31;
  wire [31:0] RegData1, RegData2, RegData3, RegData4, RegData5, RegData6, RegData7, RegData8, RegData9,
       RegData10, RegData11, RegData12, RegData13, RegData14, RegData15, RegData16, RegData17, RegData18,
       RegData19, RegData20, RegData21, RegData22, RegData23, RegData24, RegData25, RegData26, RegData27,
       RegData28, RegData29, RegData30, RegData31;

  Demultiplexer #(.select(5), .enable("false")) demultiplexer_1 (
    .out0(WrReg0), .out1(WrReg1), .out2(WrReg2), .out3(WrReg3), .out4(WrReg4), .out5(WrReg5), .out6(WrReg6),
    .out7(WrReg7), .out8(WrReg8), .out9(WrReg9), .out10(WrReg10), .out11(WrReg11), .out12(WrReg12),
    .out13(WrReg13), .out14(WrReg14), .out15(WrReg15), .out16(WrReg16), .out17(WrReg17), .out18(WrReg18),
    .out19(WrReg19), .out20(WrReg20), .out21(WrReg21), .out22(WrReg22), .out23(WrReg23), .out24(WrReg24),
    .out25(WrReg25), .out26(WrReg26), .out27(WrReg27), .out28(WrReg28), .out29(WrReg29), .out30(WrReg30),
    .out31(WrReg31), .in(WrReg), .sel(WrAddr));
  // Probe on RegData4
  Register #(.width(32)) Reg4 (.D(WrData), .en(WrReg4), .Q(RegData4), .clk(Clock));  // open: clr
  // Probe on RegData8
  Register #(.width(32)) Reg8 (.D(WrData), .en(WrReg8), .Q(RegData8), .clk(Clock));  // open: clr
  // Probe on RegData12
  Register #(.width(32)) Reg12 (.D(WrData), .en(WrReg12), .Q(RegData12), .clk(Clock));  // open: clr
  // Probe on RegData16
  Register #(.width(32)) Reg16 (.D(WrData), .en(WrReg16), .Q(RegData16), .clk(Clock));  // open: clr
  // Probe on RegData20
  Register #(.width(32)) Reg20 (.D(WrData), .en(WrReg20), .Q(RegData20), .clk(Clock));  // open: clr
  // Probe on RegData24
  Register #(.width(32)) Reg24 (.D(WrData), .en(WrReg24), .Q(RegData24), .clk(Clock));  // open: clr
  // Probe on RegData28
  Register #(.width(32)) Reg28 (.D(WrData), .en(WrReg28), .Q(RegData28), .clk(Clock));  // open: clr
  Register #(.width(32)) Reg1 (.D(WrData), .en(WrReg1), .Q(RegData1), .clk(Clock));  // open: clr
  Register #(.width(32)) Reg5 (.D(WrData), .en(WrReg5), .Q(RegData5), .clk(Clock));  // open: clr
  Register #(.width(32)) Reg9 (.D(WrData), .en(WrReg9), .Q(RegData9), .clk(Clock));  // open: clr
  Register #(.width(32)) Reg13 (.D(WrData), .en(WrReg13), .Q(RegData13), .clk(Clock));  // open: clr
  Register #(.width(32)) Reg17 (.D(WrData), .en(WrReg17), .Q(RegData17), .clk(Clock));  // open: clr
  Register #(.width(32)) Reg21 (.D(WrData), .en(WrReg21), .Q(RegData21), .clk(Clock));  // open: clr
  Register #(.width(32)) Reg25 (.D(WrData), .en(WrReg25), .Q(RegData25), .clk(Clock));  // open: clr
  Register #(.width(32)) Reg29 (.D(WrData), .en(WrReg29), .Q(RegData29), .clk(Clock));  // open: clr
  // Probe on RegData1
  // Probe on RegData5
  // Probe on RegData9
  // Probe on RegData13
  // Probe on RegData17
  // Probe on RegData21
  // Probe on RegData25
  // Probe on RegData29
  // Probe on RegData2
  Register #(.width(32)) Reg2 (.D(WrData), .en(WrReg2), .Q(RegData2), .clk(Clock));  // open: clr
  // Probe on RegData6
  Register #(.width(32)) Reg6 (.D(WrData), .en(WrReg6), .Q(RegData6), .clk(Clock));  // open: clr
  // Probe on RegData10
  Register #(.width(32)) Reg10 (.D(WrData), .en(WrReg10), .Q(RegData10), .clk(Clock));  // open: clr
  // Probe on RegData14
  Register #(.width(32)) Reg14 (.D(WrData), .en(WrReg14), .Q(RegData14), .clk(Clock));  // open: clr
  // Probe on RegData18
  Register #(.width(32)) Reg18 (.D(WrData), .en(WrReg18), .Q(RegData18), .clk(Clock));  // open: clr
  // Probe on RegData22
  Register #(.width(32)) Reg22 (.D(WrData), .en(WrReg22), .Q(RegData22), .clk(Clock));  // open: clr
  // Probe on RegData26
  Register #(.width(32)) Reg26 (.D(WrData), .en(WrReg26), .Q(RegData26), .clk(Clock));  // open: clr
  // Probe on RegData30
  Register #(.width(32)) Reg30 (.D(WrData), .en(WrReg30), .Q(RegData30), .clk(Clock));  // open: clr
  // Probe on RegData3
  Register #(.width(32)) Reg3 (.D(WrData), .en(WrReg3), .Q(RegData3), .clk(Clock));  // open: clr
  // Probe on RegData7
  Register #(.width(32)) Reg7 (.D(WrData), .en(WrReg7), .Q(RegData7), .clk(Clock));  // open: clr
  // Probe on RegData11
  Register #(.width(32)) Reg11 (.D(WrData), .en(WrReg11), .Q(RegData11), .clk(Clock));  // open: clr
  // Probe on RegData15
  Register #(.width(32)) Reg15 (.D(WrData), .en(WrReg15), .Q(RegData15), .clk(Clock));  // open: clr
  // Probe on RegData19
  Register #(.width(32)) Reg19 (.D(WrData), .en(WrReg19), .Q(RegData19), .clk(Clock));  // open: clr
  // Probe on RegData23
  Register #(.width(32)) Reg23 (.D(WrData), .en(WrReg23), .Q(RegData23), .clk(Clock));  // open: clr
  // Probe on RegData27
  Register #(.width(32)) Reg27 (.D(WrData), .en(WrReg27), .Q(RegData27), .clk(Clock));  // open: clr
  // Probe on RegData31
  Register #(.width(32)) Reg31 (.D(WrData), .en(WrReg31), .Q(RegData31), .clk(Clock));  // open: clr
  Multiplexer #(.select(5), .width(32), .enable("false")) multiplexer_1 (
    .in0({32{1'b0}}), .in1(RegData1), .in2(RegData2), .in3(RegData3), .in4(RegData4), .in5(RegData5),
    .in6(RegData6), .in7(RegData7), .in8(RegData8), .in9(RegData9), .in10(RegData10), .in11(RegData11),
    .in12(RegData12), .in13(RegData13), .in14(RegData14), .in15(RegData15), .in16(RegData16),
    .in17(RegData17), .in18(RegData18), .in19(RegData19), .in20(RegData20), .in21(RegData21),
    .in22(RegData22), .in23(RegData23), .in24(RegData24), .in25(RegData25), .in26(RegData26),
    .in27(RegData27), .in28(RegData28), .in29(RegData29), .in30(RegData30), .in31(RegData31), .out(RdData1),
    .sel(RdAddr1));
  Multiplexer #(.select(5), .width(32), .enable("false")) multiplexer_2 (
    .in0({32{1'b0}}), .in1(RegData1), .in2(RegData2), .in3(RegData3), .in4(RegData4), .in5(RegData5),
    .in6(RegData6), .in7(RegData7), .in8(RegData8), .in9(RegData9), .in10(RegData10), .in11(RegData11),
    .in12(RegData12), .in13(RegData13), .in14(RegData14), .in15(RegData15), .in16(RegData16),
    .in17(RegData17), .in18(RegData18), .in19(RegData19), .in20(RegData20), .in21(RegData21),
    .in22(RegData22), .in23(RegData23), .in24(RegData24), .in25(RegData25), .in26(RegData26),
    .in27(RegData27), .in28(RegData28), .in29(RegData29), .in30(RegData30), .in31(RegData31), .out(RdData2),
    .sel(RdAddr2));
endmodule

module Overflow_Unit (
  input  Add,
  input  Sub,
  input  ASign,
  input  BSign,
  input  ResultSign,
  output Overflow
);

  wire and_1_out, and_2_out, or_1_out, xnor_1_out, xor_1_out, xor_2_out;

  xnor xnor_1 (xnor_1_out, ASign, BSign);
  xor xor_1 (xor_1_out, ASign, BSign);
  and and_1 (and_1_out, xnor_1_out, Add);
  and and_2 (and_2_out, xor_1_out, Sub);
  or or_1 (or_1_out, and_1_out, and_2_out);
  xor xor_2 (xor_2_out, ResultSign, ASign);
  and and_3 (Overflow, or_1_out, xor_2_out);

  // Notes on the sheet:
  //   Overflow occurs when doing addition and sign(A) == sign(B) && sign(result) != sign(A)
  //   Or
  //   Overflow occurs when doing subtraction and sign(A) != sign(B) && sign(result) != sign(A)
endmodule

// CU
module Control_Unit (
  input  [5:0] Opcode,
  input  [5:0] Func,
  input  zero,
  output [2:0] ALUCtl,
  output [1:0] PCSel,
  output [1:0] DataSel,
  output Immediate,
  output [1:0] RegSel,
  output MemRd,
  output BSel,
  output MemWr,
  output WrReg
);

  wire and_4_out, Beq, beq_t, F, J, Jr, or_1_out, SW_out;

  and and_1 (Immediate, Opcode[3], ~Opcode[5]);  // AND_Gate
  and and_2 (DataSel[0], Opcode[0], Opcode[1], ~Opcode[2], ~Opcode[3], ~Opcode[4], Opcode[5]);  // AND_Gate
  and and_3 (MemWr, Opcode[0], Opcode[1], ~Opcode[2], Opcode[3], ~Opcode[4], Opcode[5]);  // AND_Gate
  and and_4 (and_4_out, ~Func[0], ~Func[1], ~Func[2], Func[3], ~Func[4], ~Func[5]);  // AND_Gate
  and and_5 (F, ~Opcode[0], ~Opcode[1], ~Opcode[2], ~Opcode[3], ~Opcode[4], ~Opcode[5]);  // AND_Gate
  and u_beq (beq_t, ~Opcode[0], ~Opcode[1], Opcode[2], ~Opcode[3], ~Opcode[4], ~Opcode[5]);  // AND_Gate
  and u_J (J, ~Opcode[0], Opcode[1], ~Opcode[2], ~Opcode[3], ~Opcode[4], ~Opcode[5]);  // AND_Gate
  and SW (SW_out, Opcode[0], Opcode[1], ~Opcode[2], Opcode[3], ~Opcode[4], Opcode[5]);  // AND_Gate
  and Jal (DataSel[1], Opcode[0], Opcode[1], ~Opcode[2], ~Opcode[3], ~Opcode[4], ~Opcode[5]);  // AND_Gate
  ALUCTL aluctl_1 (
    .ALICtl2(ALUCtl[2]), .ALICtl1(ALUCtl[1]), .ALICtl0(ALUCtl[0]), .f(F), .f3(Func[3]), .f2(Func[2]),
    .f1(Func[1]), .f0(Func[0]), .op2(Opcode[2]), .op1(Opcode[1]), .op0(Opcode[0]), .op3(Opcode[3]));
  and u_Jr (Jr, and_4_out, F);
  or or_1 (or_1_out, Jr, beq_t, J, SW_out);
  not not_1 (WrReg, or_1_out);
  PCSel pcsel_1 (.Jr(Jr), .J(J), .Jal(DataSel[1]), .Beq(Beq), .PC1(PCSel[1]), .PC0(PCSel[0]));
  and and_6 (Beq, beq_t, zero);
  or or_2 (RegSel[0], Immediate, DataSel[0]);
  or or_3 (BSel, Immediate, DataSel[0], MemWr, J);

  assign MemRd = DataSel[0];
  assign RegSel[1] = DataSel[1];

  // Other names for the same wires on the sheet: load = DataSel[0]; f0 = Func[0]; f1 = Func[1]; f2 = Func[2];
  //   f3 = Func[3]; f4 = Func[4]; f5 = Func[5]; I = Immediate; Op0 = Opcode[0]; Op1 = Opcode[1]; Op2 = Opcode[2];
  //   Op3 = Opcode[3]; Op4 = Opcode[4]; Op5 = Opcode[5]; jal = DataSel[1]; store = MemWr

  // Notes on the sheet:
  //   lw
  //   sw
endmodule

module ALUCTL (
  input  f,
  input  op3,
  input  op2,
  input  op1,
  input  op0,
  input  f3,
  input  f2,
  input  f1,
  input  f0,
  output ALICtl2,
  output ALICtl1,
  output ALICtl0
);

  wire and_1_out, and_2_out, and_3_out, and_4_out, and_5_out, and_6_out, and_7_out, and_8_out, and_9_out,
       and_10_out, and_11_out, and_12_out, and_13_out, not_1_out, not_2_out, not_3_out, not_4_out, not_5_out,
       not_6_out, not_7_out, not_8_out, not_9_out, not_10_out, not_11_out, or_1_out, or_2_out, or_3_out,
       or_4_out, or_5_out;

  not not_1 (not_1_out, op3);
  not not_2 (not_2_out, op1);
  not not_3 (not_3_out, op1);
  not not_4 (not_4_out, op0);
  not not_5 (not_5_out, op3);
  not not_6 (not_6_out, op2);
  and and_1 (and_1_out, not_1_out, not_2_out);
  and and_2 (and_2_out, not_3_out, op0);
  and and_3 (and_3_out, op1, not_4_out);
  or or_1 (or_1_out, not_5_out, not_6_out);
  and and_4 (and_4_out, f2, f1);
  not not_7 (not_7_out, f3);
  not not_8 (not_8_out, f2);
  not not_9 (not_9_out, f3);
  not not_10 (not_10_out, f2);
  not not_11 (not_11_out, f3);
  or or_2 (or_2_out, and_2_out, and_3_out);
  or or_3 (or_3_out, and_4_out, f3);
  or or_4 (or_4_out, f0, and_5_out);
  and and_5 (and_5_out, not_7_out, not_8_out, f1);
  and and_6 (and_6_out, not_9_out, not_10_out);
  or or_5 (or_5_out, and_6_out, and_7_out);
  and and_7 (and_7_out, not_11_out, f1);
  and and_8 (and_8_out, and_1_out, ~f);  // AND_Gate
  and and_9 (and_9_out, or_2_out, ~f);  // AND_Gate
  and and_10 (and_10_out, or_1_out, ~f);  // AND_Gate
  and and_11 (and_11_out, or_3_out, f);
  and and_12 (and_12_out, or_4_out, f);
  and and_13 (and_13_out, or_5_out, f);
  or or_6 (ALICtl2, and_8_out, and_11_out);
  or or_7 (ALICtl1, and_9_out, and_12_out);
  or or_8 (ALICtl0, and_10_out, and_13_out);
  // Probe on nothing
endmodule

module PCSel (
  input  Jr,
  input  J,
  input  Jal,
  input  Beq,
  output PC1,
  output PC0
);

  wire and_1_out, and_2_out, and_3_out, and_4_out, and_5_out, not_1_out, not_2_out, not_3_out, not_4_out,
       not_5_out, not_6_out, not_7_out, not_8_out, not_9_out, not_10_out, not_11_out, not_12_out, not_13_out,
       not_14_out, not_15_out;

  not not_1 (not_1_out, Jr);
  not not_2 (not_2_out, J);
  not not_3 (not_3_out, Beq);
  not not_4 (not_4_out, Jr);
  not not_5 (not_5_out, Jal);
  not not_6 (not_6_out, Beq);
  not not_7 (not_7_out, J);
  not not_8 (not_8_out, Jal);
  not not_9 (not_9_out, Beq);
  not not_10 (not_10_out, Jr);
  not not_11 (not_11_out, J);
  not not_12 (not_12_out, Jal);
  not not_13 (not_13_out, J);
  not not_14 (not_14_out, Jal);
  not not_15 (not_15_out, Beq);
  and and_1 (and_1_out, not_1_out, not_2_out, Jal, not_3_out);
  and and_2 (and_2_out, not_4_out, J, not_5_out, not_6_out);
  or or_1 (PC1, and_1_out, and_2_out, and_3_out);
  and and_3 (and_3_out, Jr, not_7_out, not_8_out, not_9_out);
  and and_4 (and_4_out, not_10_out, not_11_out, not_12_out, Beq);
  or or_2 (PC0, and_4_out, and_5_out);
  and and_5 (and_5_out, Jr, not_13_out, not_14_out, not_15_out);
endmodule
