// Logisim project Lab 3.circ as structural Verilog: 14 circuits, main circuit Main
module Main (
);

  wire beq, BF1, BF2, BSel, CLK, comparator_1_eq, control_unit_1_bsel, control_unit_1_memrd,
       control_unit_1_memwr, control_unit_1_wrreg, ex_mem_1_wrreg_2, flush_1_flush, id_ex_1_memrd_2,
       id_ex_1_memwr_2, id_ex_1_wrreg_2, J, Jr, MemRd, MemWr, mux_1_bsel_2, mux_1_memrd_2, mux_1_memwr_2,
       mux_1_wrreg_2, not_1_out, Stall, Taken, WrReg;
  wire [1:0] control_unit_1_datasel, control_unit_1_regsel, DataSel, ex_mem_1_datasel_2, FA, FB,
       id_ex_1_datasel_2, mux_1_regsel_2, RegSel;
  wire [2:0] ALUctl, control_unit_1_aluctl, mux_1_aluctl;
  wire [4:0] ex_mem_1_wraddr_2, id_ex_1_rd_2, id_ex_1_rs_2, id_ex_1_rt_2, multiplexer_6_out, rs, rt, Shamt,
       WrAddr;
  wire [5:0] Opcode;
  wire [15:0] addr;
  wire [31:0] adder_1_out, alu_1_aluresult, bit_extender_1_out, Branch, DataExt, ex_mem_1_aluresult_2,
       ex_mem_1_pc_4_2, ex_mem_1_rddata2_2, id_ex_1_dataext_2, id_ex_1_out_17, id_ex_1_out_18,
       id_ex_1_pc_4_2, if_id_1_pc_4_2, jmpAddr, jrAddr, mem_wb_1_aluresult_2, mem_wb_1_memdata_2,
       mem_wb_1_pc_4_2, MemData, multiplexer_1_out, multiplexer_2_out, multiplexer_5_out, multiplexer_7_out,
       multiplexer_8_out, multiplexer_9_out, NextPC, PC, ram_1_data, RdData1, RdData2, rom_1_data,
       shifter_1_out, WriteData;

  Clock clock_1 (.out(CLK));
  Register #(.width(32)) u_PC (.D(NextPC), .en(Stall), .Q(PC), .clk(CLK));  // open: clr
  Adder #(.width(32)) adder_1 (.a(32'h4), .b(PC), .out(adder_1_out));  // open: cin, cout
  Multiplexer #(.width(32)) multiplexer_1 (
    .in0(adder_1_out), .in1(Branch), .out(multiplexer_1_out), .sel(Taken));  // open: en
  // Probe on PC
  Multiplexer #(.width(32)) multiplexer_2 (
    .in0(multiplexer_1_out), .in1(jmpAddr), .out(multiplexer_2_out), .sel(J));  // open: en
  ROM #(.dataWidth(32)) rom_1 (.addr(PC[9:2]), .data(rom_1_data));  // open: sel
  Multiplexer #(.width(32)) multiplexer_3 (.in0(multiplexer_2_out), .in1(jrAddr), .out(NextPC), .sel(Jr));  // open: en
  Flush flush_1 (.Taken(Taken), .Jump(J), .Jr(Jr), .Flush(flush_1_flush));
  IF_ID if_id_1 (
    .Instruction(rom_1_data), .Instruction_2({Opcode, rs, rt, addr}), .CLK(CLK), .PC_4(adder_1_out),
    .PC_4_2(if_id_1_pc_4_2), .Enable(Stall), .Flush(flush_1_flush));
  // Probe on {Opcode, rs, rt, addr}
  Stall stall_1 (
    .stall(Stall), .MemRd(id_ex_1_memrd_2), .ID_EX_Rt(id_ex_1_rt_2), .IF_ID_Rs(rs), .IF_ID_Rt(rt),
    .Ex_MemRd(MemRd), .Jr(Jr), .beq(beq));
  assign bit_extender_1_out = {{6{1'b0}}, {rs, rt, addr}};  // Bit_Extender bit_extender_1
  Adder #(.width(32)) adder_2 (.a(if_id_1_pc_4_2), .b(shifter_1_out), .out(Branch));  // open: cin, cout
  Shifter #(.width(32)) shifter_1 (.in(DataExt), .\dist (5'b00010), .out(shifter_1_out));
  Shifter #(.width(32)) shifter_2 (.in(bit_extender_1_out), .\dist (5'b00010), .out(jmpAddr));
  IDForwading idforwading_1 (
    .Rs(rs), .Rt(rt), .E_M_Rd(multiplexer_6_out), .E_M_RegWr(id_ex_1_wrreg_2), .FA(BF1), .FB(BF2));
  // Probe on Opcode
  // Probe on addr[5:0]
  // Probe on rs
  // Probe on rt
  Multiplexer #(.width(32)) multiplexer_4 (.in0(RdData1), .in1(alu_1_aluresult), .out(jrAddr), .sel(BF1));  // open: en
  Multiplexer #(.width(32)) multiplexer_5 (
    .in0(RdData2), .in1(alu_1_aluresult), .out(multiplexer_5_out), .sel(BF2));  // open: en
  Control_Unit control_unit_1 (
    .Opcode(Opcode), .Func(addr[5:0]), .ALUCtl(control_unit_1_aluctl), .MemWr(control_unit_1_memwr),
    .MemRd(control_unit_1_memrd), .WrReg(control_unit_1_wrreg), .RegSel(control_unit_1_regsel), .J(J),
    .DataSel(control_unit_1_datasel), .BSel(control_unit_1_bsel), .BEQ(beq), .Jr(Jr));
  Register_File register_file_1 (
    .WrAddr(WrAddr), .WrData(WriteData), .WrReg(WrReg), .RdAddr1(rs), .RdAddr2(rt), .RdData1(RdData1),
    .RdData2(RdData2), .Clock(not_1_out));
  not not_1 (not_1_out, CLK);
  MUX mux_1 (
    .MemWr(control_unit_1_memwr), .MemWr_2(mux_1_memwr_2), .MemRd(control_unit_1_memrd),
    .MemRd_2(mux_1_memrd_2), .WrReg(control_unit_1_wrreg), .WrReg_2(mux_1_wrreg_2), .Enable(Stall),
    .ALU(control_unit_1_aluctl), .BSel(control_unit_1_bsel), .RegSel(control_unit_1_regsel),
    .ALUCtl(mux_1_aluctl), .BSel_2(mux_1_bsel_2), .RegSel_2(mux_1_regsel_2));
  assign DataExt = {{16{1'b0}}, addr};  // Bit_Extender bit_extender_2
  and and_1 (Taken, beq, comparator_1_eq);
  Comparator #(.width(32)) comparator_1 (.a(jrAddr), .b(multiplexer_5_out), .eq(comparator_1_eq));  // open: gt, lt
  ID_EX id_ex_1 (
    .CLK(CLK), .R1(RdData1), .out_17(id_ex_1_out_17), .R2(RdData2), .out_18(id_ex_1_out_18),
    .ALUCtl(mux_1_aluctl), .ALUCtl_2(ALUctl), .BSel(mux_1_bsel_2), .BSel_2(BSel), .MemWr(mux_1_memwr_2),
    .MemWr_2(id_ex_1_memwr_2), .MemRd(mux_1_memrd_2), .MemRd_2(id_ex_1_memrd_2), .WrReg(mux_1_wrreg_2),
    .WrReg_2(id_ex_1_wrreg_2), .RegSel(mux_1_regsel_2), .RegSel_2(RegSel), .DataSel(control_unit_1_datasel),
    .DataSel_2(id_ex_1_datasel_2), .DataExt(DataExt), .DataExt_2(id_ex_1_dataext_2), .rd(addr[15:11]),
    .rd_2(id_ex_1_rd_2), .rt(rt), .rt_2(id_ex_1_rt_2), .PC_4(if_id_1_pc_4_2), .PC_4_2(id_ex_1_pc_4_2),
    .Shamt(addr[10:6]), .Shamt_2(Shamt), .rs(rs), .rs_2(id_ex_1_rs_2));
  Multiplexer #(.select(2), .width(5)) multiplexer_6 (
    .in0(id_ex_1_rd_2), .in1(id_ex_1_rt_2), .in2({5{1'b1}}), .out(multiplexer_6_out), .sel(RegSel));  // open: in3, en
  Multiplexer #(.select(2), .width(32)) multiplexer_7 (
    .in0(id_ex_1_out_17), .in1(WriteData), .in2(ex_mem_1_aluresult_2), .out(multiplexer_7_out), .sel(FA));  // open: in3, en
  Multiplexer #(.select(2), .width(32)) multiplexer_8 (
    .in0(id_ex_1_out_18), .in1(WriteData), .in2(ex_mem_1_aluresult_2), .out(multiplexer_8_out), .sel(FB));  // open: in3, en
  // Probe on multiplexer_7_out
  // Probe on multiplexer_9_out
  Multiplexer #(.width(32)) multiplexer_9 (
    .in0(multiplexer_8_out), .in1(id_ex_1_dataext_2), .out(multiplexer_9_out), .sel(BSel));  // open: en
  ALU alu_1 (
    .ALUCtl(ALUctl), .ALUResult(alu_1_aluresult), .A(multiplexer_7_out), .B(multiplexer_9_out), .Shamt(Shamt));  // open: Zero, Overflow
  Forwarding forwarding_1 (
    .Rs(id_ex_1_rs_2), .Rt(id_ex_1_rt_2), .M_W_Rd(WrAddr), .MW_RegWr(WrReg), .FA(FA), .FB(FB),
    .E_M_Rd(ex_mem_1_wraddr_2), .E_M_RegWr(ex_mem_1_wrreg_2), .MemWr(MemWr));
  EX_MEM ex_mem_1 (
    .CLK(CLK), .MemWr(id_ex_1_memwr_2), .MemWr_2(MemWr), .MemRd(id_ex_1_memrd_2), .MemRd_2(MemRd),
    .WrReg(id_ex_1_wrreg_2), .WrReg_2(ex_mem_1_wrreg_2), .DataSel(id_ex_1_datasel_2),
    .DataSel_2(ex_mem_1_datasel_2), .WrAddr(multiplexer_6_out), .WrAddr_2(ex_mem_1_wraddr_2),
    .RdData2(multiplexer_8_out), .RdData2_2(ex_mem_1_rddata2_2), .ALUResult(alu_1_aluresult),
    .ALUResult_2(ex_mem_1_aluresult_2), .PC_4(id_ex_1_pc_4_2), .PC_4_2(ex_mem_1_pc_4_2));
  // Probe on ex_mem_1_aluresult_2
  // Probe on ex_mem_1_rddata2_2
  // Probe on MemWr
  RAM #(.dataWidth(32), .bus("separate")) ram_1 (
    .addr(ex_mem_1_aluresult_2[9:2]), .din(ex_mem_1_rddata2_2), .data(ram_1_data), .str(MemWr), .clk(CLK),
    .ld(MemRd));  // open: sel, clr
  MEM_WB mem_wb_1 (
    .CLK(CLK), .WrReg(ex_mem_1_wrreg_2), .WrReg_2(WrReg), .DataSel(ex_mem_1_datasel_2), .DataSel_2(DataSel),
    .ALUResult(ex_mem_1_aluresult_2), .ALUResult_2(mem_wb_1_aluresult_2), .MemData(ram_1_data),
    .MemData_2(mem_wb_1_memdata_2), .PC_4(ex_mem_1_pc_4_2), .PC_4_2(mem_wb_1_pc_4_2),
    .WrAddr(ex_mem_1_wraddr_2), .WrAddr_2(WrAddr));
  Multiplexer #(.select(2), .width(32)) multiplexer_10 (
    .in0(mem_wb_1_aluresult_2), .in1(mem_wb_1_memdata_2), .in2(mem_wb_1_pc_4_2), .out(WriteData),
    .sel(DataSel));  // open: in3, en
  // Probe on WrAddr
  // Probe on WriteData
  // Probe on WrReg
  // Probe on PC
  // Probe on NextPC
  // Probe on RdData1
  // Probe on RdData2
  // Probe on MemData
  // Probe on Branch

  // Other names for the same wires on the sheet: func[5:0] = addr[5:0]; Sha[4:0] = addr[10:6]; rd[4:0] = addr[15:11]

  // Notes on the sheet:
  //   Choose next PC
  //   Intruction Mem
  //   contents of rom_1 (hex, n*v repeats v):
  //   34010001 211020 221826 2064000e 232824 aca4000b 8ca6000b c43824 10e10003 c7402a 11080001 201cffff
  //   20090001 8c0a000c ad4a0013 8c0a000c 1141fffb c000013 201bffff 23ff0018 ac1f0000 8c0b0000 1600008
  //   201affff 8000018 2019ffff 2018ffff
  //   Flush if jump occurs
  //   Stall after load
  //   Jr and Branch
  //   Stop signal when stall
  //   Data Mem
endmodule

// Forwarding Unit
module Forwarding (
  input  [4:0] Rs,
  input  [4:0] Rt,
  input  [4:0] M_W_Rd,
  input  MW_RegWr,
  input  [4:0] E_M_Rd,
  input  E_M_RegWr,
  input  MemWr,
  output [1:0] FA,
  output [1:0] FB
);

  wire comparator_1_eq, comparator_2_eq, comparator_3_eq, comparator_4_eq, comparator_5_eq, comparator_6_eq,
       EFA, EFB, MemFB, MFA, MFB;

  Comparator #(.width(5)) comparator_1 (.a(Rs), .b(M_W_Rd), .eq(comparator_1_eq));  // open: gt, lt
  Comparator #(.width(5)) comparator_2 (.a(Rt), .b(M_W_Rd), .eq(comparator_2_eq));  // open: gt, lt
  Comparator #(.width(5)) comparator_3 (.a(M_W_Rd), .b({5{1'b0}}), .eq(comparator_3_eq));  // open: gt, lt
  Comparator #(.width(5)) comparator_4 (.a(Rs), .b(E_M_Rd), .eq(comparator_4_eq));  // open: gt, lt
  Comparator #(.width(5)) comparator_5 (.a(Rt), .b(E_M_Rd), .eq(comparator_5_eq));  // open: gt, lt
  Comparator #(.width(5)) comparator_6 (.a(E_M_Rd), .b({5{1'b0}}), .eq(comparator_6_eq));  // open: gt, lt
  and and_1 (MFA, comparator_1_eq, ~comparator_3_eq, MW_RegWr);  // AND_Gate
  and and_2 (MFB, comparator_2_eq, ~comparator_3_eq, MW_RegWr);  // AND_Gate
  and and_3 (EFA, comparator_4_eq, ~comparator_6_eq, E_M_RegWr);  // AND_Gate
  and and_4 (EFB, comparator_5_eq, ~comparator_6_eq, E_M_RegWr);  // AND_Gate
  and and_5 (MemFB, comparator_5_eq, ~comparator_6_eq, MemWr);  // AND_Gate
  ROM #(.addrWidth(2), .dataWidth(2)) rom_1 (.addr({MFA, EFA}), .data(FA));  // open: sel
  ROM #(.addrWidth(3), .dataWidth(2)) rom_2 (.addr({MFB, EFB, MemFB}), .data(FB));  // open: sel

  // Notes on the sheet:
  //   contents of rom_1 (hex, n*v repeats v):
  //   0 2 1 2
  //   contents of rom_2 (hex, n*v repeats v):
  //   0 2 2 2 1 2 2 2
endmodule

// IDForwarding
module IDForwading (
  input  [4:0] Rs,
  input  [4:0] Rt,
  input  [4:0] E_M_Rd,
  input  E_M_RegWr,
  output FA,
  output FB
);

  wire comparator_1_eq, comparator_2_eq, comparator_3_eq;

  Comparator #(.width(5)) comparator_1 (.a(Rs), .b(E_M_Rd), .eq(comparator_1_eq));  // open: gt, lt
  Comparator #(.width(5)) comparator_2 (.a(Rt), .b(E_M_Rd), .eq(comparator_2_eq));  // open: gt, lt
  Comparator #(.width(5)) comparator_3 (.a(E_M_Rd), .b({5{1'b0}}), .eq(comparator_3_eq));  // open: gt, lt
  and and_1 (FA, comparator_1_eq, ~comparator_3_eq, E_M_RegWr);  // AND_Gate
  and and_2 (FB, comparator_2_eq, ~comparator_3_eq, E_M_RegWr);  // AND_Gate

  // Other names for the same wires on the sheet: EFA = FA; EFB = FB
endmodule

module Stall (
  input  Jr,
  input  beq,
  input  MemRd,
  input  Ex_MemRd,
  input  [4:0] ID_EX_Rt,
  input  [4:0] IF_ID_Rs,
  input  [4:0] IF_ID_Rt,
  output stall
);

  wire and_1_out, and_2_out, comparator_1_eq, comparator_2_eq, or_1_out, or_2_out, or_3_out;

  or or_1 (or_1_out, Jr, beq);
  Comparator #(.width(5)) comparator_1 (.a(ID_EX_Rt), .b(IF_ID_Rs), .eq(comparator_1_eq));  // open: gt, lt
  Comparator #(.width(5)) comparator_2 (.a(ID_EX_Rt), .b(IF_ID_Rt), .eq(comparator_2_eq));  // open: gt, lt
  and and_1 (and_1_out, or_1_out, Ex_MemRd);
  or or_2 (or_2_out, MemRd, and_1_out);
  or or_3 (or_3_out, comparator_1_eq, comparator_2_eq);
  and and_2 (and_2_out, or_2_out, or_3_out);
  not not_1 (stall, and_2_out);
endmodule

module MUX (
  input  Enable,
  input  MemWr,
  input  MemRd,
  input  WrReg,
  input  [2:0] ALU,
  input  BSel,
  input  [1:0] RegSel,
  output MemWr_2,
  output MemRd_2,
  output WrReg_2,
  output [2:0] ALUCtl,
  output BSel_2,
  output [1:0] RegSel_2
);

  wire not_1_out;

  not not_1 (not_1_out, Enable);
  Multiplexer multiplexer_1 (.in0(MemWr), .in1(1'b0), .out(MemWr_2), .sel(not_1_out));  // open: en
  Multiplexer multiplexer_2 (.in0(MemRd), .in1(1'b0), .out(MemRd_2), .sel(not_1_out));  // open: en
  Multiplexer multiplexer_3 (.in0(WrReg), .in1(1'b0), .out(WrReg_2), .sel(not_1_out));  // open: en
  Multiplexer #(.width(3)) multiplexer_4 (.in0(ALU), .in1(3'b000), .out(ALUCtl), .sel(not_1_out));  // open: en
  Multiplexer multiplexer_5 (.in0(BSel), .in1(1'b0), .out(BSel_2), .sel(not_1_out));  // open: en
  Multiplexer #(.width(2)) multiplexer_6 (.in0(RegSel), .in1(2'b00), .out(RegSel_2), .sel(not_1_out));  // open: en
endmodule

module Flush (
  input  Taken,
  input  Jump,
  input  Jr,
  output Flush
);

  or or_1 (Flush, Taken, Jump, Jr);
endmodule

module IF_ID (
  input  Flush,
  input  CLK,
  input  Enable,
  input  [31:0] PC_4,
  input  [31:0] Instruction,
  output [31:0] PC_4_2,
  output [31:0] Instruction_2
);

  wire [31:0] multiplexer_1_out;

  Multiplexer #(.width(32)) multiplexer_1 (
    .in0(Instruction), .in1({32{1'b0}}), .out(multiplexer_1_out), .sel(Flush));  // open: en
  Register #(.width(32)) PC (.D(PC_4), .en(Enable), .Q(PC_4_2), .clk(CLK));  // open: clr
  Register #(.width(32)) u_Instruction (.D(multiplexer_1_out), .en(Enable), .Q(Instruction_2), .clk(CLK));  // open: clr
endmodule

module ID_EX (
  input  CLK,
  input  [31:0] R1,
  input  [31:0] R2,
  input  [2:0] ALUCtl,
  input  BSel,
  input  MemWr,
  input  MemRd,
  input  WrReg,
  input  [1:0] RegSel,
  input  [1:0] DataSel,
  input  [31:0] DataExt,
  input  [4:0] rd,
  input  [4:0] rt,
  input  [31:0] PC_4,
  input  [4:0] Shamt,
  input  [4:0] rs,
  output [31:0] out_17,
  output [31:0] out_18,
  output [2:0] ALUCtl_2,
  output BSel_2,
  output MemWr_2,
  output MemRd_2,
  output WrReg_2,
  output [1:0] RegSel_2,
  output [1:0] DataSel_2,
  output [31:0] DataExt_2,
  output [4:0] rd_2,
  output [4:0] rt_2,
  output [31:0] PC_4_2,
  output [4:0] Shamt_2,
  output [4:0] rs_2
);

  Register #(.width(32)) RdReg1 (.D(R1), .Q(out_17), .clk(CLK));  // open: en, clr
  Register #(.width(32)) RdReg2 (.D(R2), .Q(out_18), .clk(CLK));  // open: en, clr
  Register #(.width(3)) u_ALUCtl (.D(ALUCtl), .Q(ALUCtl_2), .clk(CLK));  // open: en, clr
  Register #(.width(1)) u_BSel (.D(BSel), .Q(BSel_2), .clk(CLK));  // open: en, clr
  Register #(.width(1)) u_MemWr (.D(MemWr), .Q(MemWr_2), .clk(CLK));  // open: en, clr
  Register #(.width(1)) u_MemRd (.D(MemRd), .Q(MemRd_2), .clk(CLK));  // open: en, clr
  Register #(.width(1)) u_WrReg (.D(WrReg), .Q(WrReg_2), .clk(CLK));  // open: en, clr
  Register #(.width(2)) u_RegSel (.D(RegSel), .Q(RegSel_2), .clk(CLK));  // open: en, clr
  Register #(.width(2)) u_DataSel (.D(DataSel), .Q(DataSel_2), .clk(CLK));  // open: en, clr
  Register #(.width(32)) u_DataExt (.D(DataExt), .Q(DataExt_2), .clk(CLK));  // open: en, clr
  Register #(.width(5)) u_rd (.D(rd), .Q(rd_2), .clk(CLK));  // open: en, clr
  Register #(.width(5)) u_rt (.D(rt), .Q(rt_2), .clk(CLK));  // open: en, clr
  Register #(.width(32)) u_PC_4 (.D(PC_4), .Q(PC_4_2), .clk(CLK));  // open: en, clr
  Register #(.width(5)) u_Shamt (.D(Shamt), .Q(Shamt_2), .clk(CLK));  // open: en, clr
  Register #(.width(5)) u_rs (.D(rs), .Q(rs_2), .clk(CLK));  // open: en, clr
endmodule

// EX/M
module EX_MEM (
  input  CLK,
  input  MemWr,
  input  MemRd,
  input  WrReg,
  input  [1:0] DataSel,
  input  [4:0] WrAddr,
  input  [31:0] ALUResult,
  input  [31:0] RdData2,
  input  [31:0] PC_4,
  output MemWr_2,
  output MemRd_2,
  output WrReg_2,
  output [1:0] DataSel_2,
  output [4:0] WrAddr_2,
  output [31:0] ALUResult_2,
  output [31:0] RdData2_2,
  output [31:0] PC_4_2
);

  Register #(.width(1)) u_MemWr (.D(MemWr), .Q(MemWr_2), .clk(CLK));  // open: en, clr
  Register #(.width(1)) u_MemRd (.D(MemRd), .Q(MemRd_2), .clk(CLK));  // open: en, clr
  Register #(.width(1)) u_WrReg (.D(WrReg), .Q(WrReg_2), .clk(CLK));  // open: en, clr
  Register #(.width(2)) u_DataSel (.D(DataSel), .Q(DataSel_2), .clk(CLK));  // open: en, clr
  Register #(.width(5)) u_WrAddr (.D(WrAddr), .Q(WrAddr_2), .clk(CLK));  // open: en, clr
  Register #(.width(32)) u_ALUResult (.D(ALUResult), .Q(ALUResult_2), .clk(CLK));  // open: en, clr
  Register #(.width(32)) u_RdData2 (.D(RdData2), .Q(RdData2_2), .clk(CLK));  // open: en, clr
  Register #(.width(32)) u_PC_4 (.D(PC_4), .Q(PC_4_2), .clk(CLK));  // open: en, clr
endmodule

// M/WB
module MEM_WB (
  input  CLK,
  input  WrReg,
  input  [1:0] DataSel,
  input  [31:0] ALUResult,
  input  [31:0] MemData,
  input  [31:0] PC_4,
  input  [4:0] WrAddr,
  output WrReg_2,
  output [1:0] DataSel_2,
  output [31:0] ALUResult_2,
  output [31:0] MemData_2,
  output [31:0] PC_4_2,
  output [4:0] WrAddr_2
);

  Register #(.width(1)) u_WrReg (.D(WrReg), .Q(WrReg_2), .clk(CLK));  // open: en, clr
  Register #(.width(2)) u_DataSel (.D(DataSel), .Q(DataSel_2), .clk(CLK));  // open: en, clr
  Register #(.width(32)) u_ALUResult (.D(ALUResult), .Q(ALUResult_2), .clk(CLK));  // open: en, clr
  Register #(.width(32)) u_MemData (.D(MemData), .Q(MemData_2), .clk(CLK));  // open: en, clr
  Register #(.width(32)) u_PC_4 (.D(PC_4), .Q(PC_4_2), .clk(CLK));  // open: en, clr
  Register #(.width(5)) u_WrAddr (.D(WrAddr), .Q(WrAddr_2), .clk(CLK));  // open: en, clr
endmodule

// CU
module Control_Unit (
  input  [5:0] Opcode,
  input  [5:0] Func,
  output [2:0] ALUCtl,
  output J,
  output Jr,
  output BEQ,
  output [1:0] DataSel,
  output [1:0] RegSel,
  output MemRd,
  output BSel,
  output MemWr,
  output WrReg
);

  wire and_4_out, and_6_out, and_7_out, and_8_out, and_9_out, and_10_out, and_11_out, F, I, J_t, or_1_out,
       SW_out;
  wire [2:0] rom_1_data, rom_2_data;

  and and_1 (I, Opcode[3], ~Opcode[5]);  // AND_Gate
  and and_2 (DataSel[0], Opcode[0], Opcode[1], ~Opcode[2], ~Opcode[3], ~Opcode[4], Opcode[5]);  // AND_Gate
  and and_3 (MemWr, Opcode[0], Opcode[1], ~Opcode[2], Opcode[3], ~Opcode[4], Opcode[5]);  // AND_Gate
  and and_4 (and_4_out, ~Func[0], ~Func[1], ~Func[2], Func[3], ~Func[4], ~Func[5]);  // AND_Gate
  and and_5 (F, ~Opcode[0], ~Opcode[1], ~Opcode[2], ~Opcode[3], ~Opcode[4], ~Opcode[5]);  // AND_Gate
  and u_beq (BEQ, ~Opcode[0], ~Opcode[1], Opcode[2], ~Opcode[3], ~Opcode[4], ~Opcode[5]);  // AND_Gate
  and u_J (J_t, ~Opcode[0], Opcode[1], ~Opcode[2], ~Opcode[3], ~Opcode[4], ~Opcode[5]);  // AND_Gate
  and SW (SW_out, Opcode[0], Opcode[1], ~Opcode[2], Opcode[3], ~Opcode[4], Opcode[5]);  // AND_Gate
  and Jal (DataSel[1], Opcode[0], Opcode[1], ~Opcode[2], ~Opcode[3], ~Opcode[4], ~Opcode[5]);  // AND_Gate
  and u_Jr (Jr, and_4_out, F);
  ROM #(.addrWidth(6), .dataWidth(3)) rom_1 (.addr(Func), .data(rom_1_data));  // open: sel
  ROM #(.addrWidth(6), .dataWidth(3)) rom_2 (.addr(Opcode), .data(rom_2_data));  // open: sel
  and and_6 (and_6_out, rom_2_data[2], ~F);  // AND_Gate
  and and_7 (and_7_out, rom_2_data[1], ~F);  // AND_Gate
  and and_8 (and_8_out, rom_2_data[0], ~F);  // AND_Gate
  and and_9 (and_9_out, rom_1_data[2], F);
  and and_10 (and_10_out, rom_1_data[1], F);
  and and_11 (and_11_out, rom_1_data[0], F);
  or or_1 (or_1_out, Jr, BEQ, J_t, SW_out);
  not not_1 (WrReg, or_1_out);
  or or_2 (ALUCtl[2], and_6_out, and_9_out);
  or or_3 (ALUCtl[1], and_7_out, and_10_out);
  or or_4 (ALUCtl[0], and_8_out, and_11_out);
  or or_5 (J, J_t, DataSel[1]);
  or or_6 (RegSel[0], I, DataSel[0]);
  or or_7 (BSel, I, DataSel[0], MemWr, J_t);

  assign MemRd = DataSel[0];
  assign RegSel[1] = DataSel[1];

  // Other names for the same wires on the sheet: f0 = Func[0]; f1 = Func[1]; f2 = Func[2]; f3 = Func[3]; f4 = Func[4];
  //   f5 = Func[5]; Op0 = Opcode[0]; Op1 = Opcode[1]; Op2 = Opcode[2]; Op3 = Opcode[3]; Op4 = Opcode[4];
  //   Op5 = Opcode[5]; load = DataSel[0]; jal = DataSel[1]; store = MemWr

  // Notes on the sheet:
  //   lw
  //   sw
  //   contents of rom_1 (hex, n*v repeats v):
  //   7 0 6 29*0 1 0 3 0 0 2 5 0 0 0 4
  //   contents of rom_2 (hex, n*v repeats v):
  //   8*0 1 4*0 2 21*0 1 7*0 1
endmodule

module ALU (
  input  [2:0] ALUCtl,
  input  [31:0] A,
  input  [31:0] B,
  input  [4:0] Shamt,
  output [31:0] ALUResult,
  output Zero,
  output Overflow
);

  wire comparator_1_lt, comparator_2_lt, comparator_3_eq, comparator_4_eq, or_2_out;
  wire [31:0] ADD, AND, NOR, OR, SLL, SLT, SLTU, SRL, SUB, XOR;

  assign XOR = A ^ B;  // XOR_Gate xor_1, 32 bits wide
  Adder #(.width(32)) adder_1 (.a(A), .b(B), .out(ADD));  // open: cin, cout
  Subtractor #(.width(32)) subtractor_1 (.a(A), .b(B), .out(SUB));  // open: bin, bout
  assign AND = A & B;  // AND_Gate and_1, 32 bits wide
  assign OR = A | B;  // OR_Gate or_1, 32 bits wide
  assign NOR = ~(A | B);  // NOR_Gate nor_1, 32 bits wide
  Comparator #(.width(32)) comparator_1 (.a(A), .b(B), .lt(comparator_1_lt));  // open: gt, eq
  assign SLT = {{31{1'b0}}, comparator_1_lt};  // Bit_Extender bit_extender_1
  Shifter #(.width(32)) shifter_1 (.in(B), .\dist (Shamt), .out(SLL));
  Shifter #(.width(32), .shift("lr")) shifter_2 (.in(B), .\dist (Shamt), .out(SRL));
  Comparator #(.width(32), .mode("unsigned")) comparator_2 (.a(A), .b(B), .lt(comparator_2_lt));  // open: gt, eq
  assign SLTU = {{31{1'b0}}, comparator_2_lt};  // Bit_Extender bit_extender_2
  Multiplexer #(.select(3), .width(32), .enable("false")) multiplexer_1 (
    .in0(AND), .in1(ADD), .in2(OR), .in3(SUB), .in4(SLT), .in5(XOR), .in6(SRL), .in7(SLL), .out(ALUResult),
    .sel(ALUCtl));
  Comparator #(.width(3)) comparator_3 (.a(3'b001), .b(ALUCtl), .eq(comparator_3_eq));  // open: gt, lt
  Comparator #(.width(3)) comparator_4 (.a(ALUCtl), .b(3'b011), .eq(comparator_4_eq));  // open: gt, lt
  Overflow_Unit overflow_unit_1 (
    .Add(comparator_3_eq), .Sub(comparator_4_eq), .ASign(A[31]), .BSign(B[31]), .ResultSign(ALUResult[31]),
    .Overflow(Overflow));
  not not_1 (Zero, or_2_out);
  or or_2 (or_2_out, ALUResult[0], ALUResult[1], ALUResult[2], ALUResult[3], ALUResult[4], ALUResult[5], ALUResult[6], ALUResult[7], ALUResult[8], ALUResult[9], ALUResult[10], ALUResult[11], ALUResult[12], ALUResult[13], ALUResult[14], ALUResult[15], ALUResult[16], ALUResult[17], ALUResult[18], ALUResult[19], ALUResult[20], ALUResult[21], ALUResult[22], ALUResult[23], ALUResult[24], ALUResult[25], ALUResult[26], ALUResult[27], ALUResult[28], ALUResult[29], ALUResult[30], ALUResult[31]);

  // Other names for the same wires on the sheet: ASign = A[31]; ResultSign = ALUResult[31]; BSign = B[31]

  // Notes on the sheet:
  //   ALUCtl for ADD on top port
  //   ALUCtl for SUB on second port
endmodule

module Register_File (
  input  [4:0] WrAddr,
  input  [31:0] WrData,
  input  WrReg,
  input  [4:0] RdAddr1,
  input  [4:0] RdAddr2,
  input  Clock,
  output [31:0] RdData1,
  output [31:0] RdData2
);

  wire WrReg0, WrReg1, WrReg2, WrReg3, WrReg4, WrReg5, WrReg6, WrReg7, WrReg8, WrReg9, WrReg10, WrReg11,
       WrReg12, WrReg13, WrReg14, WrReg15, WrReg16, WrReg17, WrReg18, WrReg19, WrReg20, WrReg21, WrReg22,
       WrReg23, WrReg24, WrReg25, WrReg26, WrReg27, WrReg28, WrReg29, WrReg30, WrReg31;
  wire [31:0] RegData1, RegData2, RegData3, RegData4, RegData5, RegData6, RegData7, RegData8, RegData9,
       RegData10, RegData11, RegData12, RegData13, RegData14, RegData15, RegData16, RegData17, RegData18,
       RegData19, RegData20, RegData21, RegData22, RegData23, RegData24, RegData25, RegData26, RegData27,
       RegData28, RegData29, RegData30, RegData31;

  Demultiplexer #(.select(5), .enable("false")) demultiplexer_1 (
    .out0(WrReg0), .out1(WrReg1), .out2(WrReg2), .out3(WrReg3), .out4(WrReg4), .out5(WrReg5), .out6(WrReg6),
    .out7(WrReg7), .out8(WrReg8), .out9(WrReg9), .out10(WrReg10), .out11(WrReg11), .out12(WrReg12),
    .out13(WrReg13), .out14(WrReg14), .out15(WrReg15), .out16(WrReg16), .out17(WrReg17), .out18(WrReg18),
    .out19(WrReg19), .out20(WrReg20), .out21(WrReg21), .out22(WrReg22), .out23(WrReg23), .out24(WrReg24),
    .out25(WrReg25), .out26(WrReg26), .out27(WrReg27), .out28(WrReg28), .out29(WrReg29), .out30(WrReg30),
    .out31(WrReg31), .in(WrReg), .sel(WrAddr));
  // Probe on RegData4
  Register #(.width(32)) Reg4 (.D(WrData), .en(WrReg4), .Q(RegData4), .clk(Clock));  // open: clr
  // Probe on RegData8
  Register #(.width(32)) Reg8 (.D(WrData), .en(WrReg8), .Q(RegData8), .clk(Clock));  // open: clr
  // Probe on RegData12
  Register #(.width(32)) Reg12 (.D(WrData), .en(WrReg12), .Q(RegData12), .clk(Clock));  // open: clr
  // Probe on RegData16
  Register #(.width(32)) Reg16 (.D(WrData), .en(WrReg16), .Q(RegData16), .clk(Clock));  // open: clr
  // Probe on RegData20
  Register #(.width(32)) Reg20 (.D(WrData), .en(WrReg20), .Q(RegData20), .clk(Clock));  // open: clr
  // Probe on RegData24
  Register #(.width(32)) Reg24 (.D(WrData), .en(WrReg24), .Q(RegData24), .clk(Clock));  // open: clr
  // Probe on RegData28
  Register #(.width(32)) Reg28 (.D(WrData), .en(WrReg28), .Q(RegData28), .clk(Clock));  // open: clr
  Register #(.width(32)) Reg1 (.D(WrData), .en(WrReg1), .Q(RegData1), .clk(Clock));  // open: clr
  Register #(.width(32)) Reg5 (.D(WrData), .en(WrReg5), .Q(RegData5), .clk(Clock));  // open: clr
  Register #(.width(32)) Reg9 (.D(WrData), .en(WrReg9), .Q(RegData9), .clk(Clock));  // open: clr
  Register #(.width(32)) Reg13 (.D(WrData), .en(WrReg13), .Q(RegData13), .clk(Clock));  // open: clr
  Register #(.width(32)) Reg17 (.D(WrData), .en(WrReg17), .Q(RegData17), .clk(Clock));  // open: clr
  Register #(.width(32)) Reg21 (.D(WrData), .en(WrReg21), .Q(RegData21), .clk(Clock));  // open: clr
  Register #(.width(32)) Reg25 (.D(WrData), .en(WrReg25), .Q(RegData25), .clk(Clock));  // open: clr
  Register #(.width(32)) Reg29 (.D(WrData), .en(WrReg29), .Q(RegData29), .clk(Clock));  // open: clr
  // Probe on RegData1
  // Probe on RegData5
  // Probe on RegData9
  // Probe on RegData13
  // Probe on RegData17
  // Probe on RegData21
  // Probe on RegData25
  // Probe on RegData29
  // Probe on RegData2
  Register #(.width(32)) Reg2 (.D(WrData), .en(WrReg2), .Q(RegData2), .clk(Clock));  // open: clr
  // Probe on RegData6
  Register #(.width(32)) Reg6 (.D(WrData), .en(WrReg6), .Q(RegData6), .clk(Clock));  // open: clr
  // Probe on RegData10
  Register #(.width(32)) Reg10 (.D(WrData), .en(WrReg10), .Q(RegData10), .clk(Clock));  // open: clr
  // Probe on RegData14
  Register #(.width(32)) Reg14 (.D(WrData), .en(WrReg14), .Q(RegData14), .clk(Clock));  // open: clr
  // Probe on RegData18
  Register #(.width(32)) Reg18 (.D(WrData), .en(WrReg18), .Q(RegData18), .clk(Clock));  // open: clr
  // Probe on RegData22
  Register #(.width(32)) Reg22 (.D(WrData), .en(WrReg22), .Q(RegData22), .clk(Clock));  // open: clr
  // Probe on RegData26
  Register #(.width(32)) Reg26 (.D(WrData), .en(WrReg26), .Q(RegData26), .clk(Clock));  // open: clr
  // Probe on RegData30
  Register #(.width(32)) Reg30 (.D(WrData), .en(WrReg30), .Q(RegData30), .clk(Clock));  // open: clr
  // Probe on RegData3
  Register #(.width(32)) Reg3 (.D(WrData), .en(WrReg3), .Q(RegData3), .clk(Clock));  // open: clr
  // Probe on RegData7
  Register #(.width(32)) Reg7 (.D(WrData), .en(WrReg7), .Q(RegData7), .clk(Clock));  // open: clr
  // Probe on RegData11
  Register #(.width(32)) Reg11 (.D(WrData), .en(WrReg11), .Q(RegData11), .clk(Clock));  // open: clr
  // Probe on RegData15
  Register #(.width(32)) Reg15 (.D(WrData), .en(WrReg15), .Q(RegData15), .clk(Clock));  // open: clr
  // Probe on RegData19
  Register #(.width(32)) Reg19 (.D(WrData), .en(WrReg19), .Q(RegData19), .clk(Clock));  // open: clr
  // Probe on RegData23
  Register #(.width(32)) Reg23 (.D(WrData), .en(WrReg23), .Q(RegData23), .clk(Clock));  // open: clr
  // Probe on RegData27
  Register #(.width(32)) Reg27 (.D(WrData), .en(WrReg27), .Q(RegData27), .clk(Clock));  // open: clr
  // Probe on RegData31
  Register #(.width(32)) Reg31 (.D(WrData), .en(WrReg31), .Q(RegData31), .clk(Clock));  // open: clr
  Multiplexer #(.select(5), .width(32), .enable("false")) multiplexer_1 (
    .in0({32{1'b0}}), .in1(RegData1), .in2(RegData2), .in3(RegData3), .in4(RegData4), .in5(RegData5),
    .in6(RegData6), .in7(RegData7), .in8(RegData8), .in9(RegData9), .in10(RegData10), .in11(RegData11),
    .in12(RegData12), .in13(RegData13), .in14(RegData14), .in15(RegData15), .in16(RegData16),
    .in17(RegData17), .in18(RegData18), .in19(RegData19), .in20(RegData20), .in21(RegData21),
    .in22(RegData22), .in23(RegData23), .in24(RegData24), .in25(RegData25), .in26(RegData26),
    .in27(RegData27), .in28(RegData28), .in29(RegData29), .in30(RegData30), .in31(RegData31), .out(RdData1),
    .sel(RdAddr1));
  Multiplexer #(.select(5), .width(32), .enable("false")) multiplexer_2 (
    .in0({32{1'b0}}), .in1(RegData1), .in2(RegData2), .in3(RegData3), .in4(RegData4), .in5(RegData5),
    .in6(RegData6), .in7(RegData7), .in8(RegData8), .in9(RegData9), .in10(RegData10), .in11(RegData11),
    .in12(RegData12), .in13(RegData13), .in14(RegData14), .in15(RegData15), .in16(RegData16),
    .in17(RegData17), .in18(RegData18), .in19(RegData19), .in20(RegData20), .in21(RegData21),
    .in22(RegData22), .in23(RegData23), .in24(RegData24), .in25(RegData25), .in26(RegData26),
    .in27(RegData27), .in28(RegData28), .in29(RegData29), .in30(RegData30), .in31(RegData31), .out(RdData2),
    .sel(RdAddr2));
endmodule

module Overflow_Unit (
  input  Add,
  input  Sub,
  input  ASign,
  input  BSign,
  input  ResultSign,
  output Overflow
);

  wire and_1_out, and_2_out, or_1_out, xnor_1_out, xor_1_out, xor_2_out;

  xnor xnor_1 (xnor_1_out, ASign, BSign);
  xor xor_1 (xor_1_out, ASign, BSign);
  and and_1 (and_1_out, xnor_1_out, Add);
  and and_2 (and_2_out, xor_1_out, Sub);
  or or_1 (or_1_out, and_1_out, and_2_out);
  xor xor_2 (xor_2_out, ResultSign, ASign);
  and and_3 (Overflow, or_1_out, xor_2_out);

  // Notes on the sheet:
  //   Overflow occurs when doing addition and sign(A) == sign(B) && sign(result) != sign(A)
  //   Or
  //   Overflow occurs when doing subtraction and sign(A) != sign(B) && sign(result) != sign(A)
endmodule
